# Fritzing sketch AttinyServoProgramming (saved by Fritzing 0.7.12b)
perfboards: 1

parts:
  Arduino1 = Arduino
  C1 = Electrolytic Capacitor [capacitance=10µF package="100 mil [THT, electrolytic]"]
  J1 = female pin header, 8 pins [form="♀ (female)"]
  J2 = female pin header, 5 pins [form="♀ (female)"]  # not connected
  J3 = female pin header, 5 pins [form="♀ (female)"]  # not connected
  U1 = attiny85 [package=dip]  # not connected
  J4 = screw terminal, 4 pins  # not connected

nets:
  N1: Arduino1.GND, C1.-, J1.pin1
  N2: Arduino1.D13, J1.pin4
  N3: Arduino1.D12, J1.pin5
  N4: Arduino1.D11, J1.pin6
  N5: Arduino1.D10, J1.pin3
  N6: Arduino1.RST, C1.+
  N7: Arduino1.+5V, J1.pin2

notes:
  Arduino --> AttinyServo
  GND --> GND
  Power --> Vcc
  10 --> Reset
  13 --> 2
  12 --> 1
  11 --> 0
  Arduino 10uf Reset -> GND
