# Fritzing sketch AttinyServoProgrammingMega (saved by Fritzing 0.9.0b)
perfboards: 1

parts:
  C1 = Electrolytic Capacitor [capacitance=10µF package="100 mil [THT, electrolytic]"]
  J1 = female pin header, 8 pins [form="♀ (female)"]
  J2 = female pin header, 5 pins [form="♀ (female)"]  # not connected
  J3 = female pin header, 5 pins [form="♀ (female)"]  # not connected
  U1 = attiny85 [package=dip]  # not connected
  J4 = screw terminal, 4 pins  # not connected
  Arduino1 = Arduino Mega 2560 (Rev3)

nets:
  N1: C1.-, J1.pin1, Arduino1.GND
  N2: C1.+, Arduino1.RESET
  N3: J1.pin2, Arduino1.5V
  N4: J1.pin3, Arduino1.D53
  N5: J1.pin4, Arduino1.D50
  N6: J1.pin5, Arduino1.D51
  N7: J1.pin6, Arduino1.D52

notes:
  Arduino --> AttinyServo
  GND --> GND
  Power --> Vcc
  10 --> Reset/SS
  13 --> 2 --> SCKss
  12 --> 1 --> MISO
  11 --> 0 --> MOSI
  Arduino 10uf Reset -> GND
